// Logisim project 2^5.circ as structural Verilog: 1 circuit, main circuit mod5
module mod5 (
  input  b,
  output out_2,
  output out_3,
  output out_4,
  output out_5,
  output out_6
);

  wire and_1_out, and_2_out, and_3_out, and_4_out, clock_1_out, not_1_out, not_2_out, or_1_out, or_2_out;

  or or_1 (or_1_out, out_3, out_6);
  or or_2 (or_2_out, out_4, out_5);
  not not_1 (not_1_out, b);
  not not_2 (not_2_out, b);
  and and_1 (and_1_out, not_2_out, or_1_out);
  and and_2 (and_2_out, or_1_out, b);
  and and_3 (and_3_out, b, or_2_out);
  and and_4 (and_4_out, or_2_out, not_1_out);
  Clock clock_1 (.out(clock_1_out));
  D_Flip_Flop d_ff_1 (.clk(clock_1_out), .D(and_1_out), .Q(out_3));  // open: Qn, preset, en, reset
  D_Flip_Flop d_ff_2 (.clk(clock_1_out), .D(and_2_out), .Q(out_4));  // open: Qn, preset, en, reset
  D_Flip_Flop d_ff_3 (.clk(clock_1_out), .D(and_3_out), .Q(out_5));  // open: Qn, preset, en, reset
  D_Flip_Flop d_ff_4 (.clk(clock_1_out), .D(and_4_out), .Q(out_6));  // open: Qn, preset, en, reset

  assign out_2 = 1'b0;

  // Notes on the sheet:
  //   小心不小心并联的地方哦！！
endmodule
