// Logisim project sort_4.circ as structural Verilog: 3 circuits, main circuit 1bit_swap
module _1bit_swap (
  input  l1,
  input  l2,
  input  S,
  output O1,
  output O2
);

  wire and_1_out, and_2_out, and_3_out, and_4_out, not_1_out;

  not not_1 (not_1_out, S);
  and and_1 (and_1_out, l1, not_1_out);
  and and_2 (and_2_out, l2, S);
  and and_3 (and_3_out, not_1_out, l2);
  and and_4 (and_4_out, l1, S);
  or or_1 (O1, and_1_out, and_2_out);
  or or_2 (O2, and_3_out, and_4_out);
endmodule

module _4bit_swap (
  input  [3:0] a,
  input  [3:0] b,
  input  S,
  output [3:0] a_prime,
  output [3:0] b_prime
);

  _1bit_swap u_1bit_swap_1 (.l1(a[0]), .l2(b[0]), .S(S), .O1(a_prime[0]), .O2(b_prime[0]));
  _1bit_swap u_1bit_swap_2 (.l1(a[1]), .l2(b[1]), .S(S), .O1(a_prime[1]), .O2(b_prime[1]));
  _1bit_swap u_1bit_swap_3 (.l1(a[2]), .l2(b[2]), .S(S), .O1(a_prime[2]), .O2(b_prime[2]));
  _1bit_swap u_1bit_swap_4 (.l1(a[3]), .l2(b[3]), .S(S), .O1(a_prime[3]), .O2(b_prime[3]));

  // Notes on the sheet:
  //   swap
endmodule

module _4bit_sort (
  input  [3:0] A,
  input  [3:0] B,
  input  [3:0] C,
  input  [3:0] D,
  output [3:0] out_5,
  output [3:0] out_6,
  output [3:0] out_7,
  output [3:0] out_8
);

  wire comparator_1_lt, comparator_2_lt, comparator_3_lt, comparator_4_lt, comparator_5_lt;
  wire [3:0] A1, B1, C1, D1, n4bit_swap_1_b_prime, n4bit_swap_2_a_prime;

  Comparator #(.width(4), .mode("unsigned")) comparator_1 (.a(A), .b(B), .lt(comparator_1_lt));  // open: gt, eq
  Comparator #(.width(4), .mode("unsigned")) comparator_2 (.a(C), .b(D), .lt(comparator_2_lt));  // open: gt, eq
  _4bit_swap u_4bit_swap_1 (.a(A1), .b(C1), .S(comparator_3_lt), .a_prime(out_8), .b_prime(n4bit_swap_1_b_prime));
  Comparator #(.width(4), .mode("unsigned")) comparator_3 (.a(A1), .b(C1), .lt(comparator_3_lt));  // open: gt, eq
  _4bit_swap u_4bit_swap_2 (.a(B1), .b(D1), .S(comparator_4_lt), .a_prime(n4bit_swap_2_a_prime), .b_prime(out_5));
  Comparator #(.width(4), .mode("unsigned")) comparator_4 (.a(B1), .b(D1), .lt(comparator_4_lt));  // open: gt, eq
  // Probe on A1
  _4bit_swap u_4bit_swap_3 (.a(A), .b(B), .S(comparator_1_lt), .a_prime(A1), .b_prime(B1));
  // Probe on B1
  _4bit_swap u_4bit_swap_4 (.a(C), .b(D), .S(comparator_2_lt), .a_prime(C1), .b_prime(D1));
  // Probe on D1
  Comparator #(.width(4), .mode("unsigned")) comparator_5 (
    .a(n4bit_swap_1_b_prime), .b(n4bit_swap_2_a_prime), .lt(comparator_5_lt));  // open: gt, eq
  _4bit_swap u_4bit_swap_5 (
    .a(n4bit_swap_1_b_prime), .b(n4bit_swap_2_a_prime), .S(comparator_5_lt), .a_prime(out_7), .b_prime(out_6));

  // Notes on the sheet:
  //   a1>b1
  //   C1>D1
endmodule
