// Logisim project sums_of_zero_before_the_first_one.circ as structural Verilog: 1 circuit, main circuit main
module main (
  input  [7:0] in_1
);

  wire bitfinder_1_found;
  wire [2:0] bitfinder_1_index;
  wire [3:0] adder_1_out, bit_extender_1_out, bit_extender_2_out, subtractor_1_out;

  BitAdder bitadder_1 ();  // open: in0, out
  BitSelector bitselector_1 ();  // open: in, out, sel
  BitFinder #(.\type ("high1")) bitfinder_1 (.in(in_1), .index(bitfinder_1_index), .found(bitfinder_1_found));
  assign bit_extender_1_out = {{3{1'b0}}, bitfinder_1_found};  // Bit_Extender bit_extender_1
  assign bit_extender_2_out = {{1{1'b0}}, bitfinder_1_index};  // Bit_Extender bit_extender_2
  Adder #(.width(4)) adder_1 (.a(bit_extender_2_out), .b(bit_extender_1_out), .out(adder_1_out));  // open: cin, cout
  Subtractor #(.width(4)) subtractor_1 (.a(4'b1000), .b(adder_1_out), .out(subtractor_1_out));  // open: bin, bout
  // Probe on subtractor_1_out
endmodule
