// Logisim project test1.circ as structural Verilog: 1 circuit, main circuit main
module main (
  input  [1:0] in_1,
  input  [3:0] in_2,
  input  [1:0] in_3
);

  wire [2:0] bitadder_1_out;
  wire [3:0] bit_extender_1_out, negator_1_out, odd_parity_1_out, shifter_1_out;

  // Probe on bit_extender_1_out
  assign bit_extender_1_out = {{2{in_1[1]}}, in_1};  // Bit_Extender bit_extender_1
  Shifter #(.width(4), .shift("ar")) shifter_1 (.in(in_2), .\dist (in_3), .out(shifter_1_out));
  // Probe on negator_1_out
  Negator #(.width(4)) negator_1 (.in(bit_extender_1_out), .out(negator_1_out));
  // Probe on shifter_1_out
  // Probe on odd_parity_1_out
  assign odd_parity_1_out = negator_1_out ^ shifter_1_out;  // Odd_Parity odd_parity_1, 4 bits wide
  BitAdder #(.width(4)) bitadder_1 (.in0(odd_parity_1_out), .out(bitadder_1_out));
  // Probe on bitadder_1_out
endmodule
